# Fritzing sketch light Game prototype v2 (saved by Fritzing 0.9.4)
breadboards: 2

parts:
  Part1 = Arduino Mega 2560 (Rev3)
  LED1 = smd LED [color="Red (633nm)" package="0603 [SMD]"]
  LED2 = smd LED [color="Yellow (595nm)" package="0603 [SMD]"]
  LED3 = smd LED [color="Green (555nm)" package="0603 [SMD]"]
  LED4 = smd LED [color="Blue (430nm)" package="0603 [SMD]"]
  LED5 = smd LED [color="Red (633nm)" package="0603 [SMD]"]
  LED6 = smd LED [color="Blue (430nm)" package="0603 [SMD]"]
  LED7 = smd LED [color="Yellow (595nm)" package="0603 [SMD]"]
  LED8 = smd LED [color="Green (555nm)" package="0603 [SMD]"]
  LED10 = smd LED [color="Green (555nm)" package="0603 [SMD]"]
  LED11 = smd LED [color="Red (633nm)" package="0603 [SMD]"]
  LED12 = smd LED [color="Blue (430nm)" package="0603 [SMD]"]
  R12 = Resistor [tolerance=±5% resistance=220 package="0402 [SMD]"]
  R13 = Resistor [tolerance=±5% resistance=220 package="0402 [SMD]"]
  R14 = Resistor [tolerance=±5% resistance=220 package="0402 [SMD]"]
  R15 = Resistor [tolerance=±5% resistance=220 package="0402 [SMD]"]
  R16 = Resistor [tolerance=±5% resistance=220 package="0402 [SMD]"]
  R17 = Resistor [tolerance=±5% resistance=220 package="0402 [SMD]"]
  R18 = Resistor [tolerance=±5% resistance=220 package="0402 [SMD]"]
  R19 = Resistor [tolerance=±5% resistance=220 package="0402 [SMD]"]
  R20 = Resistor [tolerance=±5% resistance=220 package="0402 [SMD]"]
  R21 = Resistor [tolerance=±5% resistance=220 package="0402 [SMD]"]
  R22 = Resistor [tolerance=±5% resistance=220 package="0402 [SMD]"]
  R23 = Resistor [tolerance=±5% resistance=220 package="0402 [SMD]"]
  LED9 = smd LED [color="Yellow (595nm)" package="0805 [SMD]"]

nets:
  N1: Part1.GND, LED1.cathode, LED2.cathode, LED3.cathode, LED4.cathode, LED5.cathode, LED6.cathode, LED7.cathode, LED8.cathode, LED10.cathode, LED11.cathode, LED12.cathode, LED9.cathode
  N2: Part1.D13_PWM, LED11.anode, R12.Pin_0, R12.Pin_1
  N3: Part1.D12_PWM, LED12.anode, R13.Pin_0, R13.Pin_1
  N4: Part1.D11_PWM, R14.Pin_0, R14.Pin_1, LED9.anode
  N5: Part1.D10_PWM, LED10.anode, R15.Pin_0, R15.Pin_1
  N6: Part1.D9_PWM, LED5.anode, R16.Pin_0, R16.Pin_1
  N7: Part1.D8_PWM, LED6.anode, R17.Pin_0, R17.Pin_1
  N8: Part1.D2_PWM, LED3.anode, R23.Pin_0, R23.Pin_1
  N9: Part1.D3_PWM, LED4.anode, R22.Pin_0, R22.Pin_1
  N10: Part1.D4_PWM, LED2.anode, R21.Pin_0, R21.Pin_1
  N11: Part1.D5_PWM, LED1.anode, R20.Pin_0, R20.Pin_1
  N12: Part1.D6_PWM, LED8.anode, R19.Pin_0, R19.Pin_1
  N13: Part1.D7_PWM, LED7.anode, R18.Pin_0, R18.Pin_1
